# Fritzing sketch RGB-LED-Control-System (saved by Fritzing 0.9.4)
breadboards: 1

parts:
  Lolin_D1_Mini = WeMos D1 Mini
  R1 = Resistor [tolerance=±5% resistance=330 package="0805 [SMD]"]
  C1 = Electrolytic Capacitor [capacitance=100μF package="0807 [SMD, electrolytic]"]
  WS2813_RGB_LED_stripe = ws2812b [package="smd 2812b"]
  Level_shifter = Logic Level Converter
  V1 = DC Power [voltage=3.3V]
  V2 = DC Power [voltage=5.0V]

nets:
  N1: Lolin_D1_Mini.3V3, Level_shifter.LV, V1.V+
  N2: Lolin_D1_Mini.5V, Level_shifter.HV
  N3: Lolin_D1_Mini.D4, R1.Pin_0
  GND: Lolin_D1_Mini.G, Level_shifter.GND, V1.V-
  N4: R1.Pin_1, Level_shifter.TX_LV
  N5: C1.-, WS2813_RGB_LED_stripe.VSS, V2.V-
  N6: C1.+, WS2813_RGB_LED_stripe.VDD, V2.V+
  N7: WS2813_RGB_LED_stripe.DIN, Level_shifter.TX_HV

notes:
  TX_HV = TXO
  TX_LV = TXI
